# Fritzing sketch Level_sensor_schematic (saved by Fritzing 0.9.3b)

parts:
  HC-SR04_Sensor_1 = HC-SR04 Ultrasonic Distance Sensor
  U1 = NodeMCU V1.0
  OLED_I2C1 = OLED 128x64 I2C Monochrome Display

nets:
  VCC: HC-SR04_Sensor_1.VCC, U1.Vin
  N1: HC-SR04_Sensor_1.TRIG, U1.D5
  N2: HC-SR04_Sensor_1.ECHO, U1.D6
  GND: HC-SR04_Sensor_1.GND, U1.GND, OLED_I2C1.GND
  N3: U1.D1, OLED_I2C1.SCK
  N4: U1.D2, OLED_I2C1.SDA
  3V3: U1.3V3, OLED_I2C1.VDD

custom parts:
  NodeMCU V1.0: ESP8266 based NodeMCU
